# Fritzing sketch TA (saved by Fritzing 0.9.3b)
breadboards: 1

parts:
  Display1 = LCD screen 16x2 IIC [part_number=101290]
  Part1 = Arduino Uno (Rev3) - ICSP  # not connected
  Part2 = AF_mshield-v1.2_breadboard
  Mod1 = KY-015 Temperature & Humidity Sensor Module [package="Breakout board"]
  F1 = Fan - Ventilador [package=THT]
  BAT1 = BC9VPC [package=bc9vpc]
  J1 = Power Plug
  Power_plug1 = Power plug  # not connected

nets:
  GND: Display1.GND, Part2.GND, Mod1.-
  VCC: Display1.VCC, Part2.VCC, Mod1.Vin
  N1: Display1.SDA, Part2.5
  N2: Display1.SCL, Part2.6
  N3: Part2.PWM1B, Mod1.S
  N4: Part2.P1, F1.GND
  N5: Part2.P2, F1.5V
  N6: BAT1.V+, J1.PWR
  N7: BAT1.V-, J1.GND

custom parts:
  LCD screen 16x2 IIC: LCD screen with HD44780 controller enables showing text, symbols, value or anything else that comes from Croduino/Arduino. It is capable of showing 16 symbols in two lines and therefore can be used in many projects that need to send clearly visible and legible output information.. • Color of symbols: White • Backlight: Blue • Dimensions: 80 x 36 x 12 mm • Screen dimensions: 64.5 x 16 mm •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
  : motor Shield v1 Adafruit Adafruit Motor/Stepper/Servo Shield for Arduino kit [v1.2] : ID 81 : $19.50 : Adafruit Industries, Unique & fun DIY electronics and kits
  KY-015 Temperature & Humidity Sensor Module: KY-015 temperature and humidity sensor module, provides a low-latency serial interface to measure humidity and temperature.
  Fan - Ventilador: Ventilador de 2 pines, se encuentra comunmente en computadoras de escritorio
  Power Plug: Power Jack This is the standard 5.5mm barrel plug for power. This part has bendable leads (i.e. wires in the real world) to connect to wall warts or the breadboard in the standard wire end, and hidden connectors on the tip end that will connect when "plugged in" (overlapped with the jack so it appears "plugged in" in breadboard) to the modified coax jack part. Internal busses connect the two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
